# Fritzing sketch fritzing_layout (saved by Fritzing 0.9.3b)

parts:
  U1 = NodeMCU V1.0
  DS1 = DS18B20 1-Wire Temperature Sensor [part_number=DS18B20]

nets:
  N1: U1.D7, U1.RX, U1.3V3#14, DS1.DQ
  N2: U1.RST, U1.3V3#19, DS1.VDD
  GND: U1.GND, DS1.GND

custom parts:
  NodeMCU V1.0: ESP8266 based NodeMCU V1.0
